// Logisim project HalfAdder.circ as structural Verilog: 1 circuit, main circuit HalfAdder
module HalfAdder (
  input  A,
  input  B,
  output Carry,
  output O
);

  wire and_2_out, and_3_out, not_1_out, not_2_out;

  and and_1 (Carry, A, B);
  not not_1 (not_1_out, A);
  not not_2 (not_2_out, B);
  and and_2 (and_2_out, not_1_out, B);
  and and_3 (and_3_out, A, not_2_out);
  or or_1 (O, and_2_out, and_3_out);
endmodule
